# Fritzing sketch Homekit (saved by Fritzing 0.9.4)
breadboards: 1

parts:
  SparkFun_ESP32_Thing_Plus1 = SparkFun ESP32 Thing Plus [part_number=14689]
  BME280 = BME280 Breakout

nets:
  N1: SparkFun_ESP32_Thing_Plus1.SCL, BME280.SCK/SCL
  N2: SparkFun_ESP32_Thing_Plus1.SDA, BME280.SDI/SDA
  3.3V: SparkFun_ESP32_Thing_Plus1.3.3V, BME280.3.3V
  GND: SparkFun_ESP32_Thing_Plus1.GND, BME280.GND

custom parts:
  SparkFun ESP32 Thing Plus: The SparkFun ESP32 Thing Plus enjoys all the amenities of the ESP32 Thing, but with a few added sparkles. We've lengthened the board just a bit to accommodate a Qwiic connector for all your Qwiic breakout needs. We've also moved a few pins around to make the board compatible with the Adafruit Huzzah32 – ESP32 Feather Board such that you can use all of those lovely shields available out there!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
